# Fritzing sketch PCB Entier (saved by Fritzing 0.9.1b)
circuit board: 3.53266cm x 20.0335cm
breadboards: 1

parts:
  LED4 = RGB LED (com. anode, rbg) [package="5 mm [THT]"]
  LED18 = RGB LED (com. anode, rbg) [package="5 mm [THT]"]
  LED19 = RGB LED (com. anode, rbg) [package="5 mm [THT]"]
  LED23 = RGB LED (com. anode, rbg) [package="5 mm [THT]"]  # not connected
  LED25 = RGB LED (com. anode, rbg) [package="5 mm [THT]"]  # not connected
  LED26 = RGB LED (com. anode, rbg) [package="5 mm [THT]"]  # not connected
  LED27 = RGB LED (com. anode, rbg) [package="5 mm [THT]"]  # not connected
  J15 = female pin header, 2 pins [form="♀ (female)"]
  R1 = Resistor [tolerance=±5% resistance=220 package="0603 [SMD]"]
  R2 = Resistor [tolerance=±5% resistance=220 package="0603 [SMD]"]
  R3 = Resistor [tolerance=±5% resistance=220 package="0603 [SMD]"]
  R4 = Resistor [tolerance=±5% resistance=220 package="0603 [SMD]"]
  R5 = Resistor [tolerance=±5% resistance=220 package="0603 [SMD]"]
  R6 = Resistor [tolerance=±5% resistance=220 package="0603 [SMD]"]
  R7 = Resistor [tolerance=±5% resistance=220 package="0603 [SMD]"]
  R8 = Resistor [tolerance=±5% resistance=220 package="0603 [SMD]"]
  R18 = Resistor [tolerance=±5% resistance=220 package="0603 [SMD]"]  # not connected
  R20 = Resistor [tolerance=±5% resistance=220 package="0603 [SMD]"]  # not connected
  R21 = Resistor [tolerance=±5% resistance=220 package="0603 [SMD]"]  # not connected
  R22 = Resistor [tolerance=±5% resistance=220 package="0603 [SMD]"]  # not connected
  R23 = Resistor [tolerance=±5% resistance=220 package="0603 [SMD]"]  # not connected
  R24 = Resistor [tolerance=±5% resistance=220 package="0603 [SMD]"]  # not connected
  R25 = Resistor [tolerance=±5% resistance=220 package="0603 [SMD]"]  # not connected
  R26 = Resistor [tolerance=±5% resistance=220 package="0603 [SMD]"]  # not connected
  U2 = 74HC595 [package="DIP16 [THT]"]
  J16 = female pin header, 3 pins [form="♀ (female)"]

nets:
  N1: LED4.red_cathode, R2.Pin_0
  N2: LED4.common_anode, LED18.common_anode, J15.pin1, U2.MR, U2.VCC
  N3: LED4.blue_cathode, R1.Pin_0
  N4: LED4.green_cathode, R3.Pin_0
  N5: LED18.red_cathode, R4.Pin_0
  N6: LED18.blue_cathode, R5.Pin_0
  N7: LED18.green_cathode, R7.Pin_0
  N8: LED19.red_cathode, R8.Pin_0
  N9: LED19.blue_cathode, R6.Pin_0
  N10: J15.pin2, U2.GND, U2.OE
  N11: R1.Pin_1, U2.Q5
  N12: R2.Pin_1, U2.Q0
  N13: R3.Pin_1, U2.Q6
  N14: R5.Pin_1, U2.Q4
  N15: R6.Pin_1, U2.Q1
  N16: R7.Pin_1, U2.Q3
  N17: R8.Pin_1, U2.Q2
  N18: U2.SH_CP, J16.pin1
  N19: U2.ST_CP, J16.pin3
  N20: U2.DS, J16.pin2
