# Fritzing sketch PCB Led Drivers horizontaux (saved by Fritzing 0.9.1b)
circuit board: 3.15899cm x 19.9923cm
breadboards: 1

parts:
  LED4 = RGB LED (com. anode, rbg) [package="5 mm [THT]"]
  LED18 = RGB LED (com. anode, rbg) [package="5 mm [THT]"]
  LED19 = RGB LED (com. anode, rbg) [package="5 mm [THT]"]
  J15 = female pin header, 2 pins [form="♀ (female)"]
  J16 = female pin header, 3 pins [form="♀ (female)"]
  R40 = Resistor [tolerance=±5% resistance=220 package=THT]
  IC1 = IC, DIP package, 16 pins [chip_label=IC]
  C1 = Tantalum Capacitor [capacitance=1μF package="100 mil [THT, tantalum]"]
  C2 = Ceramic Capacitor [capacitance=100nF package="100 mil [THT, multilayer]"]
  LED21 = RGB LED (com. anode, rbg) [package="5 mm [THT]"]
  LED23 = RGB LED (com. anode, rbg) [package="5 mm [THT]"]
  LED24 = RGB LED (com. anode, rbg) [package="5 mm [THT]"]
  R41 = Resistor [tolerance=±5% resistance=220 package=THT]
  IC2 = IC, DIP package, 16 pins [chip_label=IC]
  C3 = Tantalum Capacitor [capacitance=1μF package="100 mil [THT, tantalum]"]
  C4 = Ceramic Capacitor [capacitance=100nF package="100 mil [THT, multilayer]"]
  LED25 = RGB LED (com. anode, rbg) [package="5 mm [THT]"]
  LED27 = RGB LED (com. anode, rbg) [package="5 mm [THT]"]
  R42 = Resistor [tolerance=±5% resistance=220 package=THT]
  IC3 = IC, DIP package, 16 pins [chip_label=IC]
  C5 = Tantalum Capacitor [capacitance=1μF package="100 mil [THT, tantalum]"]
  C6 = Ceramic Capacitor [capacitance=100nF package="100 mil [THT, multilayer]"]
  LED28 = RGB LED (com. anode, rbg) [package="5 mm [THT]"]
  LED29 = RGB LED (com. anode, rbg) [package="5 mm [THT]"]
  LED30 = RGB LED (com. anode, rbg) [package="5 mm [THT]"]
  LED31 = RGB LED (com. anode, rbg) [package="5 mm [THT]"]
  LED32 = RGB LED (com. anode, rbg) [package="5 mm [THT]"]
  LED33 = RGB LED (com. anode, rbg) [package="5 mm [THT]"]
  R43 = Resistor [tolerance=±5% resistance=220 package=THT]
  R44 = Resistor [tolerance=±5% resistance=220 package=THT]
  IC4 = IC, DIP package, 16 pins [chip_label=IC]
  IC5 = IC, DIP package, 16 pins [chip_label=IC]
  C7 = Tantalum Capacitor [capacitance=1μF package="100 mil [THT, tantalum]"]
  C8 = Tantalum Capacitor [capacitance=1μF package="100 mil [THT, tantalum]"]
  C9 = Ceramic Capacitor [capacitance=100nF package="100 mil [THT, multilayer]"]
  C10 = Ceramic Capacitor [capacitance=100nF package="100 mil [THT, multilayer]"]
  LED34 = RGB LED (com. anode, rbg) [package="5 mm [THT]"]
  LED36 = RGB LED (com. anode, rbg) [package="5 mm [THT]"]
  R45 = Resistor [tolerance=±5% resistance=220 package=THT]
  IC6 = IC, DIP package, 16 pins [chip_label=IC]
  C11 = Tantalum Capacitor [capacitance=1μF package="100 mil [THT, tantalum]"]
  C12 = Ceramic Capacitor [capacitance=100nF package="100 mil [THT, multilayer]"]

nets:
  N1: LED4.red_cathode, IC1.pin5
  N2: LED4.common_anode, LED18.common_anode, LED19.common_anode, J15.pin1, IC1.pin16, C1.-, C2.0, LED21.common_anode, LED23.common_anode, LED24.common_anode, R41.Pin_1, IC2.pin1, IC2.pin13, C3.-, C4.0, LED25.common_anode, LED27.common_anode, R42.Pin_1, IC3.pin1, IC3.pin13, C5.-, C6.0, R43.Pin_1, R44.Pin_1, IC4.pin1, IC4.pin13, IC5.pin1, IC5.pin13, C7.-, C8.-, C9.0, C10.0, R45.Pin_1, IC6.pin1, IC6.pin13
  N3: LED4.blue_cathode, IC1.pin6
  N4: LED4.green_cathode, IC1.pin7
  N5: LED18.red_cathode, IC1.pin8
  N6: LED18.blue_cathode, IC1.pin9
  N7: LED18.green_cathode, IC1.pin10
  N8: LED19.red_cathode, IC1.pin11
  N9: LED19.blue_cathode, IC1.pin12
  N10: LED19.green_cathode, IC2.pin5
  N11: J15.pin2, R40.Pin_1, IC1.pin1, IC1.pin13, C1.+, C2.1, IC2.pin16, C3.+, C4.1, IC3.pin16, C5.+, C6.1, LED28.common_anode, LED29.common_anode, LED30.common_anode, LED31.common_anode, LED32.common_anode, LED33.common_anode, IC4.pin16, IC5.pin16, C7.+, C8.+, C9.1, C10.1, LED34.common_anode, LED36.common_anode, IC6.pin16, C11.+, C12.1
  N12: J16.pin1, IC1.pin2
  N13: J16.pin2, IC1.pin3, IC2.pin3, IC3.pin3, IC4.pin3, IC5.pin3, IC6.pin3
  N14: J16.pin3, IC1.pin4, IC2.pin4, IC3.pin4, IC4.pin4, IC5.pin4, IC6.pin4
  N15: R40.Pin_0, IC1.pin15
  N16: IC1.pin14, IC2.pin2
  N17: LED21.red_cathode, IC2.pin12
  N18: LED21.blue_cathode, IC3.pin5
  N19: LED21.green_cathode, IC3.pin6
  N20: LED23.red_cathode, IC2.pin9
  N21: LED23.blue_cathode, IC2.pin10
  N22: LED23.green_cathode, IC2.pin11
  N23: LED24.red_cathode, IC2.pin6
  N24: LED24.blue_cathode, IC2.pin7
  N25: LED24.green_cathode, IC2.pin8
  N26: R41.Pin_0, IC2.pin15
  N27: IC2.pin14, IC3.pin2
  N28: LED25.red_cathode, IC3.pin7
  N29: LED25.blue_cathode, IC3.pin8
  N30: LED25.green_cathode, IC3.pin9
  N31: LED27.red_cathode, IC3.pin10
  N32: LED27.blue_cathode, IC3.pin11
  N33: LED27.green_cathode, IC3.pin12
  N34: R42.Pin_0, IC3.pin15
  N35: IC3.pin14, IC4.pin2
  N36: LED28.red_cathode, IC5.pin6
  N37: LED28.blue_cathode, IC5.pin7
  N38: LED28.green_cathode, IC5.pin8
  N39: LED29.red_cathode, IC4.pin11
  N40: LED29.blue_cathode, IC4.pin12
  N41: LED29.green_cathode, IC5.pin5
  N42: LED30.red_cathode, IC5.pin12
  N43: LED30.blue_cathode, IC6.pin5
  N44: LED30.green_cathode, IC6.pin6
  N45: LED31.red_cathode, IC4.pin8
  N46: LED31.blue_cathode, IC4.pin9
  N47: LED31.green_cathode, IC4.pin10
  N48: LED32.red_cathode, IC5.pin9
  N49: LED32.blue_cathode, IC5.pin10
  N50: LED32.green_cathode, IC5.pin11
  N51: LED33.red_cathode, IC4.pin5
  N52: LED33.blue_cathode, IC4.pin6
  N53: LED33.green_cathode, IC4.pin7
  N54: R43.Pin_0, IC4.pin15
  N55: R44.Pin_0, IC5.pin15
  N56: IC4.pin14, IC5.pin2
  N57: IC5.pin14, IC6.pin2
  N58: LED34.red_cathode, IC6.pin7
  N59: LED34.blue_cathode, IC6.pin8
  N60: LED34.green_cathode, IC6.pin9
  N61: LED36.red_cathode, IC6.pin10
  N62: LED36.blue_cathode, IC6.pin11
  N63: LED36.green_cathode, IC6.pin12
  N64: R45.Pin_0, IC6.pin15
  N65: C11.-, C12.0
